// Logisim project y86.circ as structural Verilog: 2 circuits, main circuit main
module main (
  input  Reset
);

  wire and_1_out, Clock_out, imem_1_p3, imem_1_p4, imem_1_p5, imem_1_p6, imem_1_p7, imem_1_p8, imem_1_p9,
       imem_1_p10, imem_1_p11, imem_1_p12, nor_1_out, not_1_out;
  wire [1:0] imem_1_p17, Stat_q;
  wire [7:0] imem_1_p1;
  wire [31:0] adder_1_out, PC_q, undriven;

  and and_1 (and_1_out, Clock_out, nor_1_out);
  Clock Clock (.out(Clock_out));
  Adder adder_1 (.a(undriven[7:0]), .b(imem_1_p1), .out(adder_1_out[7:0]));  // open: cin, cout
  Register #(.width(32)) PC (.D(undriven), .Q(PC_q), .clk(and_1_out), .clr(Reset));  // open: en
  nor nor_1 (nor_1_out, Stat_q[1], Stat_q[0]);
  not not_1 (not_1_out, and_1_out);
  Register #(.width(2)) Stat (.D(imem_1_p17), .Q(Stat_q), .clk(not_1_out));  // open: en, clr
  // imem imem_1: pin names not known; wires that end beside it: imem_1_p1, PC_q, imem_1_p3, imem_1_p4, imem_1_p5, imem_1_p6, imem_1_p7, imem_1_p8, imem_1_p9, imem_1_p10, imem_1_p11, imem_1_p12, imem_1_p3, imem_1_p4, imem_1_p5, imem_1_p6, imem_1_p17, imem_1_p7, imem_1_p8, imem_1_p9, imem_1_p10, imem_1_p11, imem_1_p12
  Register #(.width(32)) PChold (.Q(adder_1_out), .clk(not_1_out), .clr(Reset));  // open: D, en
  // Pins of 8 and 32 bits meet at adder_1_out
  // Pins of 8 and 32 bits meet at undriven

  // Notes on the sheet:
  //   PC Increment
  //   Memory
  //   Add the current value of the program counter to the length of the instruction
  //   Val P
endmodule

module Align (
  input  [7:0] B1,
  input  [7:0] B2,
  input  [7:0] B3,
  input  [7:0] B4,
  input  [7:0] B5,
  input  [7:0] B6,
  input  [7:0] B7,
  input  [7:0] B8,
  input  [7:0] B9,
  input  NeedRegs,
  output [3:0] rA,
  output [3:0] rB,
  output [31:0] valC_1,
  output [31:0] valC_0
);
endmodule
